// Logisim project gpu.circ as structural Verilog: 1 circuit, main circuit main
module main (
);

  wire button_1_out, clock_1_out, comparator_1_lt, comparator_2_lt, comparator_3_lt, nor_1_out;
  wire [9:0] bit_extender_1_out, bit_extender_2_out, subtractor_1_out, subtractor_2_out, subtractor_3_out,
       subtractor_4_out, subtractor_5_out, subtractor_6_out, subtractor_7_out, subtractor_8_out,
       subtractor_9_out, subtractor_10_out, subtractor_11_out, subtractor_12_out;
  wire [13:0] counter_1_q;
  wire [15:0] bit_extender_3_out, bit_extender_4_out, bit_extender_5_out, bit_extender_6_out,
       bit_extender_7_out, bit_extender_8_out, bit_extender_9_out, bit_extender_10_out, bit_extender_11_out,
       bit_extender_12_out, bit_extender_13_out, bit_extender_14_out, multiplier_1_out, multiplier_2_out,
       multiplier_3_out, multiplier_4_out, multiplier_5_out, multiplier_6_out, subtractor_13_out,
       subtractor_14_out, subtractor_15_out;
  wire [23:0] multiplexer_1_out;

  Button button_1 (.out(button_1_out));
  Clock clock_1 (.out(clock_1_out));
  Counter #(.max('h3fff), .width(14)) counter_1 (
    .Q(counter_1_q), .clk(clock_1_out), .clr(button_1_out));  // open: load, D, count, carry
  assign bit_extender_1_out = {{3{1'b0}}, counter_1_q[6:0]};  // Bit_Extender bit_extender_1
  assign bit_extender_2_out = {{3{1'b0}}, counter_1_q[13:7]};  // Bit_Extender bit_extender_2
  Subtractor #(.width(10)) subtractor_1 (.a(bit_extender_1_out), .b(10'h8), .out(subtractor_1_out));  // open: bin, bout
  Subtractor #(.width(10)) subtractor_2 (.a(bit_extender_2_out), .b(10'h5), .out(subtractor_2_out));  // open: bin, bout
  Subtractor #(.width(10)) subtractor_3 (.a(10'h8), .b(10'h70), .out(subtractor_3_out));  // open: bin, bout
  Subtractor #(.width(10)) subtractor_4 (.a(10'h5), .b(10'h65), .out(subtractor_4_out));  // open: bin, bout
  // Probe on counter_1_q[6:0]
  Subtractor #(.width(10)) subtractor_5 (
    .a(bit_extender_1_out), .b(10'h10), .out(subtractor_5_out));  // open: bin, bout
  Subtractor #(.width(10)) subtractor_6 (
    .a(bit_extender_2_out), .b(10'h42), .out(subtractor_6_out));  // open: bin, bout
  Subtractor #(.width(10)) subtractor_7 (.a(10'h10), .b(10'h8), .out(subtractor_7_out));  // open: bin, bout
  Subtractor #(.width(10)) subtractor_8 (.a(10'h42), .b(10'h5), .out(subtractor_8_out));  // open: bin, bout
  // Probe on counter_1_q[13:7]
  Subtractor #(.width(10)) subtractor_9 (
    .a(bit_extender_1_out), .b(10'h70), .out(subtractor_9_out));  // open: bin, bout
  Subtractor #(.width(10)) subtractor_10 (
    .a(bit_extender_2_out), .b(10'h65), .out(subtractor_10_out));  // open: bin, bout
  Subtractor #(.width(10)) subtractor_11 (.a(10'h70), .b(10'h10), .out(subtractor_11_out));  // open: bin, bout
  Subtractor #(.width(10)) subtractor_12 (.a(10'h65), .b(10'h42), .out(subtractor_12_out));  // open: bin, bout
  assign bit_extender_3_out = {{6{subtractor_9_out[9]}}, subtractor_9_out};  // Bit_Extender bit_extender_3
  assign bit_extender_4_out = {{6{subtractor_5_out[9]}}, subtractor_5_out};  // Bit_Extender bit_extender_4
  assign bit_extender_5_out = {{6{subtractor_1_out[9]}}, subtractor_1_out};  // Bit_Extender bit_extender_5
  assign bit_extender_6_out = {{6{subtractor_10_out[9]}}, subtractor_10_out};  // Bit_Extender bit_extender_6
  assign bit_extender_7_out = {{6{subtractor_6_out[9]}}, subtractor_6_out};  // Bit_Extender bit_extender_7
  assign bit_extender_8_out = {{6{subtractor_2_out[9]}}, subtractor_2_out};  // Bit_Extender bit_extender_8
  assign bit_extender_9_out = {{6{subtractor_11_out[9]}}, subtractor_11_out};  // Bit_Extender bit_extender_9
  assign bit_extender_10_out = {{6{subtractor_7_out[9]}}, subtractor_7_out};  // Bit_Extender bit_extender_10
  assign bit_extender_11_out = {{6{subtractor_3_out[9]}}, subtractor_3_out};  // Bit_Extender bit_extender_11
  assign bit_extender_12_out = {{6{subtractor_12_out[9]}}, subtractor_12_out};  // Bit_Extender bit_extender_12
  assign bit_extender_13_out = {{6{subtractor_8_out[9]}}, subtractor_8_out};  // Bit_Extender bit_extender_13
  assign bit_extender_14_out = {{6{subtractor_4_out[9]}}, subtractor_4_out};  // Bit_Extender bit_extender_14
  Multiplier #(.width(16)) multiplier_1 (
    .a(bit_extender_5_out), .b(bit_extender_13_out), .out(multiplier_1_out));  // open: cin, cout
  Multiplier #(.width(16)) multiplier_2 (
    .a(bit_extender_8_out), .b(bit_extender_10_out), .out(multiplier_2_out));  // open: cin, cout
  Multiplier #(.width(16)) multiplier_3 (
    .a(bit_extender_4_out), .b(bit_extender_12_out), .out(multiplier_3_out));  // open: cin, cout
  Multiplier #(.width(16)) multiplier_4 (
    .a(bit_extender_7_out), .b(bit_extender_9_out), .out(multiplier_4_out));  // open: cin, cout
  Multiplier #(.width(16)) multiplier_5 (
    .a(bit_extender_3_out), .b(bit_extender_14_out), .out(multiplier_5_out));  // open: cin, cout
  Multiplier #(.width(16)) multiplier_6 (
    .a(bit_extender_6_out), .b(bit_extender_11_out), .out(multiplier_6_out));  // open: cin, cout
  Subtractor #(.width(16)) subtractor_13 (
    .a(multiplier_1_out), .b(multiplier_2_out), .out(subtractor_13_out));  // open: bin, bout
  Subtractor #(.width(16)) subtractor_14 (
    .a(multiplier_3_out), .b(multiplier_4_out), .out(subtractor_14_out));  // open: bin, bout
  Subtractor #(.width(16)) subtractor_15 (
    .a(multiplier_5_out), .b(multiplier_6_out), .out(subtractor_15_out));  // open: bin, bout
  Comparator #(.width(16)) comparator_1 (.a(subtractor_13_out), .b({16{1'b0}}), .lt(comparator_1_lt));  // open: gt, eq
  Comparator #(.width(16)) comparator_2 (.a(subtractor_14_out), .b({16{1'b0}}), .lt(comparator_2_lt));  // open: gt, eq
  Comparator #(.width(16)) comparator_3 (.a(subtractor_15_out), .b({16{1'b0}}), .lt(comparator_3_lt));  // open: gt, eq
  nor nor_1 (nor_1_out, comparator_3_lt, comparator_2_lt, comparator_1_lt);
  Multiplexer #(.enable("false"), .width(24)) multiplexer_1 (
    .in0({24{1'b0}}), .in1(24'hf33c4d), .out(multiplexer_1_out), .sel(nor_1_out));
  // RGB_Video rgb_video_1: pin names not known; wires that end beside it: button_1_out, clock_1_out, 1'b1, counter_1_q[6:0], counter_1_q[13:7], multiplexer_1_out

  // Notes on the sheet:
  //   X
  //   P
  //   Y
  //   V0
  //   X
  //   V1
  //   Y
  //   V2
  //   Color
  //   X
  //   Y
  //   X
  //   Y
  //   Y
  //   X
  //   i
  //   e
  //   a
  //   k
  //   g
  //   c
  //   h
  //   d
  //   l
  //   f
  //   b
  //   j
  //   TRIANGLE RASTERIZER
  //   m
  //   n
  //   o
  //   p
  //   q
  //   r
  //   s
  //   t
  //   u
endmodule
